# Fritzing sketch Fritzing (saved by Fritzing 1.0.4)
breadboards: 2

parts:
  Mod1 = STM32F303
  Componente2 = Motor Driver 1A Dual TB6612FNG
  M1 = gear-motor

nets:
  N1: Mod1.A0, Componente2.PWMA
  N2: Mod1.A1, Componente2.AIN1
  N3: Mod1.A2, Componente2.AIN2
  N4: Mod1.A3, Componente2.PWMB
  N5: Mod1.A4, Componente2.BIN1
  N6: Mod1.A5, Componente2.BIN2
  N7: Mod1.A6, Componente2.STBY
  GND: Mod1.GND, Componente2.GND
  5V: Mod1.5V, Componente2.VCC
  N8: Componente2.A02, M1.pin_2
  N9: Componente2.A01, M1.pin_1

custom parts:
  STM32F303: Medium density Cortex-M3 microcontroller.
